# Fritzing sketch CircuitDiagram_Rev002 (saved by Fritzing 0.8.7b)
breadboards: 1

parts:
  Gas_Sensor-1 = MQ-4
  Part2 = Arduino Nano (Rev3.0)
  Bulk_Voltage(Step_Down) = Mini-360 DC-DC Buck converter [package=THT]
  Gas_Sensor_2 = MQ-4
  Flame_Sensor-1 = KY-026
  Flame_Sensor-2 = KY-026
  M1 = sim800L v2 evb
  LCM1602_IIC2 = LCM1602 IIC [part_number="LCM1602 IIC" chip_label="LCM1602 IIC" package="DIP (Dual Inline) [THT]"]
  LCD_16x2 = LCD screen
  Relay_Module = Jtron 1 Channel Optoisolated Relay Module [package=relay]
  reset_sw = Round Pushbutton
  ESP8266 = ESP8266 NodeMCU LoLin module

nets:
  VCC: Gas_Sensor-1.VCC, Part2.VIN, Bulk_Voltage(Step_Down).OUT+, Gas_Sensor_2.VCC, Flame_Sensor-1.pin3, Flame_Sensor-2.pin3, M1.pin_7, LCM1602_IIC2.VCC, ESP8266.Vin
  GND: Gas_Sensor-1.GND, Part2.GND, Bulk_Voltage(Step_Down).OUT-, Gas_Sensor_2.GND, Flame_Sensor-1.pin2, Flame_Sensor-2.pin2, M1.pin_2, M1.pin_6, LCM1602_IIC2.GND, Relay_Module.GND, reset_sw.leg1, ESP8266.GND
  N1: Gas_Sensor-1.AO, Part2.A0
  N2: Part2.D1/TX, ESP8266.D2
  N3: Part2.D0/RX, ESP8266.D3
  N4: Part2.RESET, reset_sw.leg0
  N5: Part2.D2, M1.pin_4
  N6: Part2.D3, M1.pin_3
  N7: Part2.D5, Flame_Sensor-1.pin4
  N8: Part2.D6, Flame_Sensor-2.pin4
  N9: Part2.D11/MOSI, Relay_Module.IN1
  N10: Part2.A5, LCM1602_IIC2.SCL
  N11: Part2.A4, LCM1602_IIC2.SDA
  N12: Part2.A1, Gas_Sensor_2.AO
  VSS: LCM1602_IIC2.VSS, LCD_16x2.VSS
  VDD: LCM1602_IIC2.VDD, LCD_16x2.VDD
  N13: LCM1602_IIC2.V0, LCD_16x2.V0
  N14: LCM1602_IIC2.RS, LCD_16x2.RS
  N15: LCM1602_IIC2.RW, LCD_16x2.R/W
  N16: LCM1602_IIC2.E, LCD_16x2.E
  N17: LCM1602_IIC2.D0, LCD_16x2.DB0
  N18: LCM1602_IIC2.D1, LCD_16x2.DB1
  N19: LCM1602_IIC2.D2, LCD_16x2.DB2
  N20: LCM1602_IIC2.D3, LCD_16x2.DB3
  N21: LCM1602_IIC2.D4, LCD_16x2.DB4
  N22: LCM1602_IIC2.D5, LCD_16x2.DB5
  N23: LCM1602_IIC2.D6, LCD_16x2.DB6
  N24: LCM1602_IIC2.D7, LCD_16x2.DB7
  N25: LCM1602_IIC2.A, LCD_16x2.LED+
  N26: LCM1602_IIC2.K, LCD_16x2.LED-

custom parts:
  Mini-360 DC-DC Buck converter: Mini-360 DC-DC Buck converter. Tiny buck step down voltage converter, input voltage 4.75 to 23V output 1 to 17V adjustable. Available from ebay and the like.
  KY-026: ky-026 flame sensor module
  sim800L v2 evb: sim800L v2 evb GSM module.
  LCM1602 IIC: I2C-Module to use a 1602 or 2004 LCD on with the wire.h libory Serial LCD Modul
  ESP8266 NodeMCU LoLin module: ESP8266 based NodeMCU
